# Fritzing sketch RPi-button-led (saved by Fritzing 0.9.2b)
breadboards: 1

parts:
  Pi1 = Adafruit Pi Cobbler
  R1 = Resistor [tolerance=±5% resistance=220 package="0603 [SMD]"]
  LED1 = smd LED [color="Red (633nm)" package="0805 [SMD]"]
  S1 = Pushbutton [package="[SMD]"]
  R2 = Resistor [tolerance=±5% resistance=10k package="0603 [SMD]"]

nets:
  N1: Pi1.3V3, S1.Pin_1, S1.Pin_2
  N2: Pi1.GND, R1.Pin_0, R2.Pin_0
  N3: Pi1.#18, LED1.anode
  N4: Pi1.#23, S1.Pin_3, S1.Pin_4, R2.Pin_1
  N5: R1.Pin_1, LED1.cathode

custom parts:
  Adafruit Pi Cobbler: Adafruit Pi Cobbler GPIO Breakout for Raspberry Pi
