# Fritzing sketch RPi-led (saved by Fritzing 0.9.2b)
breadboards: 1

parts:
  Pi1 = Adafruit Pi Cobbler
  R1 = Resistor [tolerance=±5% resistance=220 package="0603 [SMD]"]
  LED1 = smd LED [color="Red (633nm)" package="0805 [SMD]"]

nets:
  N1: Pi1.GND, R1.Pin_0
  N2: Pi1.#18, LED1.anode
  N3: R1.Pin_1, LED1.cathode

custom parts:
  Adafruit Pi Cobbler: Adafruit Pi Cobbler GPIO Breakout for Raspberry Pi
