# Fritzing sketch RBL_BLE_Shield_Temperature (saved by Fritzing 0.9.3b)
breadboards: 1

parts:
  Part1 = MCP9808 High Accuracy I2C Temperature Sensor [part_number=1782]
  Bluetooth_Low_Energy_Shield_V2_1 = Bluetooth Low Energy Shield V2.1
  Part2 = Arduino Uno (Rev3) - ICSP  # not connected

nets:
  VDD: Part1.VDD, Bluetooth_Low_Energy_Shield_V2_1.5V
  GND: Part1.GND, Bluetooth_Low_Energy_Shield_V2_1.GND
  N1: Part1.SCL, Bluetooth_Low_Energy_Shield_V2_1.SCL
  N2: Part1.SDA, Bluetooth_Low_Energy_Shield_V2_1.SDA

custom parts:
  MCP9808 High Accuracy I2C Temperature Sensor: This I2C digital temperature sensor is one of the more accurate/precise we've ever seen, with a typical accuracy of ±0.25°C over the sensor's -40°C to +125°C range and precision of +0.0625°C. They work great with any microcontroller using standard i2c. There are 3 address pins so you can connect up to 8 to a single I2C bus without address collisions. Best of all, a wide voltage range makes is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
  Bluetooth Low Energy Shield V2.1: BLE Shield stands for Bluetooth Low Energy (BLE) Shield. It is designed to work with Arduino boards or compatibles, including Arduino Uno, Mega 2560, Leonardo and Due. It allows you to connect your Arduino boards with other BLE Central device like a smartphone or tablet. BLE shield could operate under 3.3V or 5V, therefore it works with a lot of Arduino compatible boards too.
