# Fritzing sketch NeoPixel_101 (saved by Fritzing 0.9.3b)

parts:
  neopixel1 = Neopixel Ring 16
  Part2 = Arduino 101

nets:
  VCC: neopixel1.VCC, Part2.5V
  N1: neopixel1.IN, Part2.D6_PWM
  N2: neopixel1.OUT, Part2.GND

custom parts:
  Neopixel Ring 16: Neopixel Ring x16
  Arduino 101: A learning and development board that delivers the performance and low-power consumption of the Intel® Curie™ Module with the simplicity of Arduino at an entry-level price. It keeps the same robust form factor and peripheral list of the UNO with the addition of onboard Bluetooth LE capabilities and a 6-axis accelerometer/gyro to help you easily expand your creativity into the connected world.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
