# Fritzing sketch LED (saved by Fritzing 0.9.3b)
breadboards: 1

parts:
  Part1 = Arduino 101
  LED1 = smd LED [color="Red (633nm)" package="1206 [SMD]"]
  R2 = Resistor [tolerance=±5% resistance=330 package=THT]

nets:
  N1: Part1.GND, R2.Pin_1
  N2: Part1.D6_PWM, LED1.anode
  N3: LED1.cathode, R2.Pin_0

custom parts:
  Arduino 101: A learning and development board that delivers the performance and low-power consumption of the Intel® Curie™ Module with the simplicity of Arduino at an entry-level price. It keeps the same robust form factor and peripheral list of the UNO with the addition of onboard Bluetooth LE capabilities and a 6-axis accelerometer/gyro to help you easily expand your creativity into the connected world.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
