# Fritzing sketch Thermometer (saved by Fritzing 0.9.3b)
breadboards: 1

parts:
  Part1 = Arduino 101
  LED1 = smd LED [color="Red (633nm)" package="1206 [SMD]"]
  R2 = Resistor [tolerance=±5% resistance=330 package=THT]
  R3 = Resistor [tolerance=±5% resistance=10k package=THT]
  S1 = Pushbutton [package="[THT]"]
  U1 = TMP36 [package=to-92]

nets:
  N1: Part1.A0, U1.VOUT
  GND: Part1.GND, R2.Pin_1, R3.Pin_1, U1.GND
  N2: Part1.D6_PWM, LED1.anode
  N3: Part1.D7, R3.Pin_0, S1.Pin_3, S1.Pin_4
  3V3: Part1.3V3, S1.Pin_1, S1.Pin_2, U1.VCC
  N4: LED1.cathode, R2.Pin_0

custom parts:
  Arduino 101: A learning and development board that delivers the performance and low-power consumption of the Intel® Curie™ Module with the simplicity of Arduino at an entry-level price. It keeps the same robust form factor and peripheral list of the UNO with the addition of onboard Bluetooth LE capabilities and a 6-axis accelerometer/gyro to help you easily expand your creativity into the connected world.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
