# Fritzing sketch NeoPixel (saved by Fritzing 0.9.3b)

parts:
  RF1 = nRF8001 Bluetooth LE Breakout
  Part1 = Arduino Uno (Rev3)
  neopixel1 = Neopixel Ring 16

nets:
  N1: RF1.SCK, Part1.D13/SCK
  N2: RF1.MISO, Part1.D12/MISO
  N3: RF1.MOSI, Part1.D11_PWM/MOSI
  N4: RF1.REQ, Part1.D10_PWM/SS
  N5: RF1.RDY, Part1.D2
  N6: RF1.RST, Part1.D9_PWM
  GND: RF1.GND, Part1.GND, neopixel1.GND
  VIN: RF1.VIN, Part1.5V, neopixel1.VCC
  N7: Part1.D6_PWM, neopixel1.IN

custom parts:
  nRF8001 Bluetooth LE Breakout: nRF8001 Breakout Board
  Neopixel Ring 16: Neopixel Ring x16
